# Fritzing sketch PipBoy (saved by Fritzing 0.9.3b)
stripboards: 3

parts:
  Teensy1 = Teensy 3.6 (Basic)
  switch1 = Rotary_Switch_12x1
  Part1 = 3.5in TFT 480x320 Touch + MicroSD
  Part2 = PowerBoost 1000 Basic
  ENCODER1 = Rotary Encoder with Knob
  LED1 = RGB LED (com. cathode, rgb) [package="5 mm [THT]"]  # not connected
  Part4 = Adafruit FONA 808 Breakout [part_number="Adafruit #2542"]  # not connected
  R1 = Resistor [tolerance=±5% resistance=220 package="2512 [SMD]"]
  R2 = Resistor [tolerance=±5% resistance=220 package="2512 [SMD]"]
  R3 = Resistor [tolerance=±5% resistance=220 package="2512 [SMD]"]
  R4 = Resistor [tolerance=±5% resistance=220 package="2512 [SMD]"]
  Part5 = Mono 2.5W Class D Audio Amplifier - PAM8302
  SP1 = SPEAKER [package=pcb_mount_speaker]
  Part6 = Adafruit Audio FX Mini Sound Board [part_number="Adafruit #2342 and #2220"]
  Part3 = Adafruit Ultimate GPS v3 [part_number="Adafruit #746"]
  Part7 = Digital FM Radio Receiver  # not connected
  R5 = Resistor [tolerance=±5% resistance=10k package="0805 [SMD]"]
  R6 = Resistor [tolerance=±5% resistance=10k package="0805 [SMD]"]
  S1 = Taiway 100-SP-X-T1 SPDT Miniature Toggle Switch [part_number=100-SP-X-T1-0-0-B1-M2 package=THT]

nets:
  GND: Teensy1.GND, Teensy1.GND1, Part1.GND, Part2.GND, ENCODER1.no_name_yet#2, Part5.GND, Part6.GND, Part3.GND, S1.L1
  N1: Teensy1.D6, Part1.LCD_LITE
  N2: Teensy1.D9, Part3.TX
  N3: Teensy1.D10, Part3.RX
  N4: Teensy1.D11, Part1.MOSI
  N5: Teensy1.D12, Part1.MISO
  N6: Teensy1.D13, Part1.LCD_WR_5V
  N7: Teensy1.3V3, Teensy1.3V3_1
  VIN: Teensy1.Vin, Part1.+5V, Part2.5.0V, Part5.VCC, Part5.VO-, SP1.-, Part6.VIN, Part3.3.3V, R5.Pin_0, R6.Pin_0
  N8: Teensy1.D24, Part1.LCD_CS_5V
  N9: Teensy1.D25, Part1.LCD_RS_5V
  N10: Teensy1.D33, Part6.RX_5V
  N11: Teensy1.D34, Part6.TX
  N12: Teensy1.D35, switch1.8, R4.Pin_0
  N13: Teensy1.D36, switch1.0
  N14: Teensy1.D38, ENCODER1.no_name_yet#3, R6.Pin_1
  N15: Teensy1.D39, ENCODER1.no_name_yet#1, R5.Pin_1
  N16: switch1.9, R3.Pin_0, R4.Pin_1
  N17: switch1.10, R2.Pin_0, R3.Pin_1
  N18: switch1.11, R1.Pin_0, R2.Pin_1
  N19: switch1.12, R1.Pin_1
  N20: Part2.ENABLE, S1.COM
  N21: Part2.LBO, S1.L2
  N22: Part5.AIN-, Part5.VO+, SP1.+, Part6.R_AC
  N23: Part5.AIN+, Part6.L_AC

custom parts:
  Teensy 3.6 (Basic): The Teensy is a complete USB-based microcontoller development system, in a very small footprint, capable of implementing many types of projects. All programming is done via the USB port. No special programmer is needed, only a standard micro-USB cable and a PC or Macintosh with a USB port.
  3.5in TFT 480x320 Touch + MicroSD: This TFT display is big (3.5" diagonal), bright (6 white-LED backlight) and colorful! 480x320 pixels with individual RGB pixel control. This display also has a resistive touchscreen attached to it already, so you can detect finger presses anywhere on the screen. There is a controller built into the display with RAM buffering, so that almost no work is done by the microcontroller. The display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
  PowerBoost 1000 Basic: The PowerBoost 1000 is a little DC/DC boost converter module that can run from 1.8V batteries or higher, and convert the battery output to 5.2V DC for running your 5V projects. At its heart is a TPS61030 boost converter from TI. This boost converter chip has some really nice extras such as low battery detection, 4A internal switch, synchronous conversion, excellent efficiency, and 700KHz high-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
  Rotary Encoder with Knob: Rotary Encoder with 1/4" Shaft and Knob
  Adafruit FONA 808 Breakout: Cellular + GPS tracking, all in one? Oh yes! Introducing Adafruit FONA 808 MiniGSM + GPS, an all-in-one cellular phone module with that lets you add location-tracking, voice, text, SMS and data to your project in an adorable little package.
  Mono 2.5W Class D Audio Amplifier - PAM8302: A super small but powerful mono amplifier able to deliver up to 2.5 Watts into 4-8 ohm impedance speakers. Inside the miniature chip is a class D controller, able to run from 2.0V-5.5VDC. Since the amp is a class D, its very efficient (over 90% efficient when driving an 8Ω speaker at over half a Watt) - making it perfect for portable and battery-powered projects.
  Adafruit Audio FX Mini Sound Board: Would you like to add audio/sound effects to your next project, without an Arduino+Shield? Or maybe you don't even know how to use microcontrollers, you just want to make a sound play whenever you press a button. What about something that has to be very small and portable? You are probably feeling a little frustrated: it's been very hard to find a simple, low cost audio effects trigger that is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
  Adafruit Ultimate GPS v3: We carry a few different GPS modules here in the Adafruit shop, but none that satisfied our every desire - that's why we designed this little GPS breakout board. We believe this is the Ultimate GPS module, so we named it that. It's got everything you want and more: -165 dBm sensitivity, 10 Hz updates, 66 channels 5V friendly design and only 20mA current draw Breadboard friendly + two mounting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
